// Logisim project 07ABR-Somador.circ as structural Verilog: 4 circuits, main circuit main
module main (
  input  A,
  input  B,
  input  C,
  output C_out,
  output S
);

  wire and_1_out, and_2_out, and_3_out, xor_1_out;

  and and_1 (and_1_out, A, B);
  and and_2 (and_2_out, A, C);
  or or_1 (C_out, and_1_out, and_2_out, and_3_out);
  and and_3 (and_3_out, B, C);
  xor xor_1 (xor_1_out, B, C);
  xor xor_2 (S, xor_1_out, A);
endmodule

module somadorRippleCarry (
  input  [7:0] A,
  input  [7:0] B,
  input  in_3,
  output [7:0] S
);

  wire main_1_c_out, main_2_c_out, main_3_c_out, main_4_c_out, main_5_c_out, main_6_c_out, main_7_c_out,
       main_8_c_out;
  wire [7:0] xor_1_out;

  assign xor_1_out = B ^ {8{in_3}};  // XOR_Gate xor_1, 8 bits wide
  main main_1 (.C_out(main_1_c_out), .S(S[7]), .A(A[7]), .B(xor_1_out[7]), .C(main_2_c_out));
  main main_2 (.C_out(main_2_c_out), .S(S[6]), .A(A[6]), .B(xor_1_out[6]), .C(main_3_c_out));
  main main_3 (.C_out(main_3_c_out), .S(S[5]), .A(A[5]), .B(xor_1_out[5]), .C(main_4_c_out));
  main main_4 (.C_out(main_4_c_out), .S(S[4]), .A(A[4]), .B(xor_1_out[4]), .C(main_5_c_out));
  main main_5 (.C_out(main_5_c_out), .S(S[3]), .A(A[3]), .B(xor_1_out[3]), .C(main_6_c_out));
  main main_6 (.C_out(main_6_c_out), .S(S[2]), .A(A[2]), .B(xor_1_out[2]), .C(main_7_c_out));
  main main_7 (.C_out(main_7_c_out), .S(S[1]), .A(A[1]), .B(xor_1_out[1]), .C(main_8_c_out));
  main main_8 (.C_out(main_8_c_out), .S(S[0]), .A(A[0]), .B(xor_1_out[0]), .C(1'b0));
endmodule

module somadorComCout (
  input  A,
  input  B,
  input  C,
  output C_out,
  output S
);

  wire and_1_out, and_2_out, and_3_out, xor_1_out;

  and and_1 (and_1_out, A, B);
  or or_1 (C_out, and_1_out, and_2_out, and_3_out);
  and and_2 (and_2_out, A, C);
  and and_3 (and_3_out, B, C);
  xor xor_1 (xor_1_out, B, C);
  xor xor_2 (S, xor_1_out, A);
endmodule

module somadorSemCout (
  input  A,
  input  B,
  input  C,
  output S
);

  wire xor_1_out;

  xor xor_1 (xor_1_out, B, C);
  xor xor_2 (S, xor_1_out, A);
endmodule
