// Logisim project 07ABR.circ as structural Verilog: 2 circuits, main circuit main
module main (
  input  A,
  input  B,
  input  C,
  output S,
  output C_out
);

  wire and_1_out, and_2_out, and_3_out, xor_1_out;

  and and_1 (and_1_out, A, B);
  or or_1 (S, and_1_out, and_2_out, and_3_out);
  and and_2 (and_2_out, A, C);
  and and_3 (and_3_out, B, C);
  xor xor_1 (xor_1_out, B, C);
  xor xor_2 (C_out, xor_1_out, A);
endmodule

module somador (
  input  [7:0] A,
  input  [7:0] B,
  output [7:0] S
);

  wire main_1_c_out, main_2_c_out, main_3_c_out, main_4_c_out, main_5_c_out, main_6_c_out, main_7_c_out,
       main_8_c_out;

  main main_1 (.S(S[7]), .C_out(main_1_c_out), .A(A[7]), .B(B[7]), .C(main_2_c_out));
  main main_2 (.S(S[6]), .C_out(main_2_c_out), .A(A[6]), .B(B[6]), .C(main_3_c_out));
  main main_3 (.S(S[5]), .C_out(main_3_c_out), .A(A[5]), .B(B[5]), .C(main_4_c_out));
  main main_4 (.S(S[4]), .C_out(main_4_c_out), .A(A[4]), .B(B[4]), .C(main_5_c_out));
  main main_5 (.S(S[3]), .C_out(main_5_c_out), .A(A[3]), .B(B[3]), .C(main_6_c_out));
  main main_6 (.S(S[2]), .C_out(main_6_c_out), .A(A[2]), .B(B[2]), .C(main_7_c_out));
  main main_7 (.S(S[1]), .C_out(main_7_c_out), .A(A[1]), .B(B[1]), .C(main_8_c_out));
  main main_8 (.S(S[0]), .C_out(main_8_c_out), .A(A[0]), .B(B[0]), .C(1'b0));
endmodule
